# Fritzing sketch STET002 (saved by Fritzing 0.9.3b)
circuit board: 5cm x 6.2cm

parts:
  J1 = female pin header, 14 pins [form="♀ (female)"]
  J2 = female pin header, 14 pins [form="♀ (female)"]
  J3 = female pin header, 14 pins [form="♀ (female)"]
  J4 = female pin header, 14 pins [form="♀ (female)"]
  J5 = female pin header, 4 pins [form="♀ (female)"]
  J6 = female pin header, 6 pins [form="♀ (female)"]

nets:
  N1: J1.pin1, J2.pin1, J5.pin2, J5.pin3, J6.pin3
  N2: J1.pin2, J2.pin2, J6.pin4
  N3: J1.pin3, J2.pin3, J6.pin5
  N4: J1.pin4, J2.pin4
  N5: J1.pin5, J2.pin5
  N6: J1.pin6, J2.pin6
  N7: J1.pin7, J2.pin7
  N8: J1.pin8, J2.pin8
  N9: J1.pin9, J2.pin9
  N10: J1.pin10, J2.pin10
  N11: J1.pin11, J2.pin11
  N12: J1.pin12, J2.pin12
  N13: J1.pin13, J2.pin13
  N14: J1.pin14, J2.pin14
  N15: J3.pin1, J4.pin1, J5.pin1, J5.pin4, J6.pin2
  N16: J3.pin2, J4.pin2
  N17: J3.pin3, J4.pin3
  N18: J3.pin4, J4.pin4
  N19: J3.pin5, J4.pin5
  N20: J3.pin6, J4.pin6
  N21: J3.pin7, J4.pin7
  N22: J3.pin8, J4.pin8
  N23: J3.pin9, J4.pin9
  N24: J3.pin10, J4.pin10
  N25: J3.pin11, J4.pin11
  N26: J3.pin12, J4.pin12
  N27: J3.pin13, J4.pin13
  N28: J3.pin14, J4.pin14
